// Logisim project screen.circ as structural Verilog: 5 circuits, main circuit main
module main (
);

  wire button_1_out, Controller_draw, Controller_write;
  wire [4:0] Controller_row;
  wire [19:0] Controller_address;
  wire [31:0] counter_1_q, register_1_q, rom_1_data, rom_2_data, rom_3_data, rom_4_data,
       screenconnector2_1_out_5, screenconnector2_1_out_6, screenconnector2_1_out_7,
       screenconnector2_1_out_8, screenconnector2_1_out_9, screenconnector2_1_out_10,
       screenconnector2_1_out_11, screenconnector2_1_out_12, screenconnector2_1_out_13,
       screenconnector2_1_out_14, screenconnector2_1_out_15, screenconnector2_1_out_16,
       screenconnector2_1_out_17, screenconnector2_1_out_18, screenconnector2_1_out_19,
       screenconnector2_1_out_20, screenconnector2_1_out_21, screenconnector2_1_out_22,
       screenconnector2_1_out_23, screenconnector2_1_out_24, screenconnector2_1_out_25,
       screenconnector2_1_out_26, screenconnector2_1_out_27, screenconnector2_1_out_28,
       screenconnector2_1_out_29, screenconnector2_1_out_30, screenconnector2_1_out_31,
       screenconnector2_1_out_32, screenconnector2_1_out_33, screenconnector2_1_out_34,
       screenconnector2_1_out_35, screenconnector2_1_out_36, screenconnector2_2_out_5,
       screenconnector2_2_out_6, screenconnector2_2_out_7, screenconnector2_2_out_8,
       screenconnector2_2_out_9, screenconnector2_2_out_10, screenconnector2_2_out_11,
       screenconnector2_2_out_12, screenconnector2_2_out_13, screenconnector2_2_out_14,
       screenconnector2_2_out_15, screenconnector2_2_out_16, screenconnector2_2_out_17,
       screenconnector2_2_out_18, screenconnector2_2_out_19, screenconnector2_2_out_20,
       screenconnector2_2_out_21, screenconnector2_2_out_22, screenconnector2_2_out_23,
       screenconnector2_2_out_24, screenconnector2_2_out_25, screenconnector2_2_out_26,
       screenconnector2_2_out_27, screenconnector2_2_out_28, screenconnector2_2_out_29,
       screenconnector2_2_out_30, screenconnector2_2_out_31, screenconnector2_2_out_32,
       screenconnector2_2_out_33, screenconnector2_2_out_34, screenconnector2_2_out_35,
       screenconnector2_2_out_36, screenconnector_1_out_5, screenconnector_1_out_6, screenconnector_1_out_7,
       screenconnector_1_out_8, screenconnector_1_out_9, screenconnector_1_out_10, screenconnector_1_out_11,
       screenconnector_1_out_12, screenconnector_1_out_13, screenconnector_1_out_14,
       screenconnector_1_out_15, screenconnector_1_out_16, screenconnector_1_out_17,
       screenconnector_1_out_18, screenconnector_1_out_19, screenconnector_1_out_20,
       screenconnector_1_out_21, screenconnector_1_out_22, screenconnector_1_out_23,
       screenconnector_1_out_24, screenconnector_1_out_25, screenconnector_1_out_26,
       screenconnector_1_out_27, screenconnector_1_out_28, screenconnector_1_out_29,
       screenconnector_1_out_30, screenconnector_1_out_31, screenconnector_1_out_32,
       screenconnector_1_out_33, screenconnector_1_out_34, screenconnector_1_out_35,
       screenconnector_1_out_36, screenconnector_2_out_5, screenconnector_2_out_6, screenconnector_2_out_7,
       screenconnector_2_out_8, screenconnector_2_out_9, screenconnector_2_out_10, screenconnector_2_out_11,
       screenconnector_2_out_12, screenconnector_2_out_13, screenconnector_2_out_14,
       screenconnector_2_out_15, screenconnector_2_out_16, screenconnector_2_out_17,
       screenconnector_2_out_18, screenconnector_2_out_19, screenconnector_2_out_20,
       screenconnector_2_out_21, screenconnector_2_out_22, screenconnector_2_out_23,
       screenconnector_2_out_24, screenconnector_2_out_25, screenconnector_2_out_26,
       screenconnector_2_out_27, screenconnector_2_out_28, screenconnector_2_out_29,
       screenconnector_2_out_30, screenconnector_2_out_31, screenconnector_2_out_32,
       screenconnector_2_out_33, screenconnector_2_out_34, screenconnector_2_out_35, screenconnector_2_out_36;

  ROM #(.addrWidth(20), .dataWidth(32)) rom_1 (.addr(Controller_address), .data(rom_1_data));  // open: sel
  ROM #(.addrWidth(20), .dataWidth(32)) rom_2 (.addr(Controller_address), .data(rom_2_data));  // open: sel
  screenconnector screenconnector_1 (
    .Data(rom_1_data), .out_5(screenconnector_1_out_5), .out_6(screenconnector_1_out_6),
    .out_7(screenconnector_1_out_7), .out_8(screenconnector_1_out_8), .out_9(screenconnector_1_out_9),
    .out_10(screenconnector_1_out_10), .out_11(screenconnector_1_out_11), .out_12(screenconnector_1_out_12),
    .out_13(screenconnector_1_out_13), .out_14(screenconnector_1_out_14), .out_15(screenconnector_1_out_15),
    .out_16(screenconnector_1_out_16), .out_17(screenconnector_1_out_17), .out_18(screenconnector_1_out_18),
    .out_19(screenconnector_1_out_19), .out_20(screenconnector_1_out_20), .out_21(screenconnector_1_out_21),
    .out_22(screenconnector_1_out_22), .out_23(screenconnector_1_out_23), .out_24(screenconnector_1_out_24),
    .out_25(screenconnector_1_out_25), .out_26(screenconnector_1_out_26), .out_27(screenconnector_1_out_27),
    .out_28(screenconnector_1_out_28), .out_29(screenconnector_1_out_29), .out_30(screenconnector_1_out_30),
    .out_31(screenconnector_1_out_31), .out_32(screenconnector_1_out_32), .out_33(screenconnector_1_out_33),
    .out_34(screenconnector_1_out_34), .out_35(screenconnector_1_out_35), .out_36(screenconnector_1_out_36),
    .Row(Controller_row), .Store(Controller_write), .Draw(Controller_draw));
  DotMatrix #(.inputtype("row"), .matrixcols(32), .matrixrows(32), .persist(1)) dotmatrix_1 (
    .row0(screenconnector_1_out_5), .row1(screenconnector_1_out_6), .row2(screenconnector_1_out_7),
    .row3(screenconnector_1_out_8), .row4(screenconnector_1_out_9), .row5(screenconnector_1_out_10),
    .row6(screenconnector_1_out_11), .row7(screenconnector_1_out_12), .row8(screenconnector_1_out_13),
    .row9(screenconnector_1_out_14), .row10(screenconnector_1_out_15), .row11(screenconnector_1_out_16),
    .row12(screenconnector_1_out_17), .row13(screenconnector_1_out_18), .row14(screenconnector_1_out_19),
    .row15(screenconnector_1_out_20), .row16(screenconnector_1_out_21), .row17(screenconnector_1_out_22),
    .row18(screenconnector_1_out_23), .row19(screenconnector_1_out_24), .row20(screenconnector_1_out_25),
    .row21(screenconnector_1_out_26), .row22(screenconnector_1_out_27), .row23(screenconnector_1_out_28),
    .row24(screenconnector_1_out_29), .row25(screenconnector_1_out_30), .row26(screenconnector_1_out_31),
    .row27(screenconnector_1_out_32), .row28(screenconnector_1_out_33), .row29(screenconnector_1_out_34),
    .row30(screenconnector_1_out_35), .row31(screenconnector_1_out_36));
  screenconnector screenconnector_2 (
    .Data(rom_2_data), .out_5(screenconnector_2_out_5), .out_6(screenconnector_2_out_6),
    .out_7(screenconnector_2_out_7), .out_8(screenconnector_2_out_8), .out_9(screenconnector_2_out_9),
    .out_10(screenconnector_2_out_10), .out_11(screenconnector_2_out_11), .out_12(screenconnector_2_out_12),
    .out_13(screenconnector_2_out_13), .out_14(screenconnector_2_out_14), .out_15(screenconnector_2_out_15),
    .out_16(screenconnector_2_out_16), .out_17(screenconnector_2_out_17), .out_18(screenconnector_2_out_18),
    .out_19(screenconnector_2_out_19), .out_20(screenconnector_2_out_20), .out_21(screenconnector_2_out_21),
    .out_22(screenconnector_2_out_22), .out_23(screenconnector_2_out_23), .out_24(screenconnector_2_out_24),
    .out_25(screenconnector_2_out_25), .out_26(screenconnector_2_out_26), .out_27(screenconnector_2_out_27),
    .out_28(screenconnector_2_out_28), .out_29(screenconnector_2_out_29), .out_30(screenconnector_2_out_30),
    .out_31(screenconnector_2_out_31), .out_32(screenconnector_2_out_32), .out_33(screenconnector_2_out_33),
    .out_34(screenconnector_2_out_34), .out_35(screenconnector_2_out_35), .out_36(screenconnector_2_out_36),
    .Row(Controller_row), .Store(Controller_write), .Draw(Controller_draw));
  DotMatrix #(.inputtype("row"), .matrixcols(32), .matrixrows(32), .persist(1)) dotmatrix_2 (
    .row0(screenconnector_2_out_5), .row1(screenconnector_2_out_6), .row2(screenconnector_2_out_7),
    .row3(screenconnector_2_out_8), .row4(screenconnector_2_out_9), .row5(screenconnector_2_out_10),
    .row6(screenconnector_2_out_11), .row7(screenconnector_2_out_12), .row8(screenconnector_2_out_13),
    .row9(screenconnector_2_out_14), .row10(screenconnector_2_out_15), .row11(screenconnector_2_out_16),
    .row12(screenconnector_2_out_17), .row13(screenconnector_2_out_18), .row14(screenconnector_2_out_19),
    .row15(screenconnector_2_out_20), .row16(screenconnector_2_out_21), .row17(screenconnector_2_out_22),
    .row18(screenconnector_2_out_23), .row19(screenconnector_2_out_24), .row20(screenconnector_2_out_25),
    .row21(screenconnector_2_out_26), .row22(screenconnector_2_out_27), .row23(screenconnector_2_out_28),
    .row24(screenconnector_2_out_29), .row25(screenconnector_2_out_30), .row26(screenconnector_2_out_31),
    .row27(screenconnector_2_out_32), .row28(screenconnector_2_out_33), .row29(screenconnector_2_out_34),
    .row30(screenconnector_2_out_35), .row31(screenconnector_2_out_36));
  Counter #(.width(32), .max('hffffffff)) counter_1 (
    .Q(counter_1_q), .clk(Controller_draw));  // open: load, D, count, carry, clr
  DotMatrix #(.inputtype("row"), .matrixcols(32), .matrixrows(32), .persist(1)) dotmatrix_3 (
    .row0(screenconnector2_1_out_5), .row1(screenconnector2_1_out_6), .row2(screenconnector2_1_out_7),
    .row3(screenconnector2_1_out_8), .row4(screenconnector2_1_out_9), .row5(screenconnector2_1_out_10),
    .row6(screenconnector2_1_out_11), .row7(screenconnector2_1_out_12), .row8(screenconnector2_1_out_13),
    .row9(screenconnector2_1_out_14), .row10(screenconnector2_1_out_15), .row11(screenconnector2_1_out_16),
    .row12(screenconnector2_1_out_17), .row13(screenconnector2_1_out_18), .row14(screenconnector2_1_out_19),
    .row15(screenconnector2_1_out_20), .row16(screenconnector2_1_out_21), .row17(screenconnector2_1_out_22),
    .row18(screenconnector2_1_out_23), .row19(screenconnector2_1_out_24), .row20(screenconnector2_1_out_25),
    .row21(screenconnector2_1_out_26), .row22(screenconnector2_1_out_27), .row23(screenconnector2_1_out_28),
    .row24(screenconnector2_1_out_29), .row25(screenconnector2_1_out_30), .row26(screenconnector2_1_out_31),
    .row27(screenconnector2_1_out_32), .row28(screenconnector2_1_out_33), .row29(screenconnector2_1_out_34),
    .row30(screenconnector2_1_out_35), .row31(screenconnector2_1_out_36));
  DotMatrix #(.inputtype("row"), .matrixcols(32), .matrixrows(32), .persist(1)) dotmatrix_4 (
    .row0(screenconnector2_2_out_5), .row1(screenconnector2_2_out_6), .row2(screenconnector2_2_out_7),
    .row3(screenconnector2_2_out_8), .row4(screenconnector2_2_out_9), .row5(screenconnector2_2_out_10),
    .row6(screenconnector2_2_out_11), .row7(screenconnector2_2_out_12), .row8(screenconnector2_2_out_13),
    .row9(screenconnector2_2_out_14), .row10(screenconnector2_2_out_15), .row11(screenconnector2_2_out_16),
    .row12(screenconnector2_2_out_17), .row13(screenconnector2_2_out_18), .row14(screenconnector2_2_out_19),
    .row15(screenconnector2_2_out_20), .row16(screenconnector2_2_out_21), .row17(screenconnector2_2_out_22),
    .row18(screenconnector2_2_out_23), .row19(screenconnector2_2_out_24), .row20(screenconnector2_2_out_25),
    .row21(screenconnector2_2_out_26), .row22(screenconnector2_2_out_27), .row23(screenconnector2_2_out_28),
    .row24(screenconnector2_2_out_29), .row25(screenconnector2_2_out_30), .row26(screenconnector2_2_out_31),
    .row27(screenconnector2_2_out_32), .row28(screenconnector2_2_out_33), .row29(screenconnector2_2_out_34),
    .row30(screenconnector2_2_out_35), .row31(screenconnector2_2_out_36));
  player Controller (
    .Draw(Controller_draw), .Address(Controller_address), .Write(Controller_write), .Row(Controller_row));
  // Probe on register_1_q
  Register #(.width(32)) register_1 (.D(counter_1_q), .Q(register_1_q), .clk(button_1_out));  // open: en, clr
  Button button_1 (.out(button_1_out));
  screenconnector2 screenconnector2_1 (
    .Data(rom_3_data), .Row(Controller_row), .out_5(screenconnector2_1_out_5),
    .out_6(screenconnector2_1_out_6), .out_7(screenconnector2_1_out_7), .out_8(screenconnector2_1_out_8),
    .out_9(screenconnector2_1_out_9), .out_10(screenconnector2_1_out_10), .out_11(screenconnector2_1_out_11),
    .out_12(screenconnector2_1_out_12), .out_13(screenconnector2_1_out_13),
    .out_14(screenconnector2_1_out_14), .out_15(screenconnector2_1_out_15),
    .out_16(screenconnector2_1_out_16), .out_17(screenconnector2_1_out_17),
    .out_18(screenconnector2_1_out_18), .out_19(screenconnector2_1_out_19),
    .out_20(screenconnector2_1_out_20), .out_21(screenconnector2_1_out_21),
    .out_22(screenconnector2_1_out_22), .out_23(screenconnector2_1_out_23),
    .out_24(screenconnector2_1_out_24), .out_25(screenconnector2_1_out_25),
    .out_26(screenconnector2_1_out_26), .out_27(screenconnector2_1_out_27),
    .out_28(screenconnector2_1_out_28), .out_29(screenconnector2_1_out_29),
    .out_30(screenconnector2_1_out_30), .out_31(screenconnector2_1_out_31),
    .out_32(screenconnector2_1_out_32), .out_33(screenconnector2_1_out_33),
    .out_34(screenconnector2_1_out_34), .out_35(screenconnector2_1_out_35),
    .out_36(screenconnector2_1_out_36), .Store(Controller_write), .Draw(Controller_draw));
  screenconnector2 screenconnector2_2 (
    .Data(rom_4_data), .Row(Controller_row), .out_5(screenconnector2_2_out_5),
    .out_6(screenconnector2_2_out_6), .out_7(screenconnector2_2_out_7), .out_8(screenconnector2_2_out_8),
    .out_9(screenconnector2_2_out_9), .out_10(screenconnector2_2_out_10), .out_11(screenconnector2_2_out_11),
    .out_12(screenconnector2_2_out_12), .out_13(screenconnector2_2_out_13),
    .out_14(screenconnector2_2_out_14), .out_15(screenconnector2_2_out_15),
    .out_16(screenconnector2_2_out_16), .out_17(screenconnector2_2_out_17),
    .out_18(screenconnector2_2_out_18), .out_19(screenconnector2_2_out_19),
    .out_20(screenconnector2_2_out_20), .out_21(screenconnector2_2_out_21),
    .out_22(screenconnector2_2_out_22), .out_23(screenconnector2_2_out_23),
    .out_24(screenconnector2_2_out_24), .out_25(screenconnector2_2_out_25),
    .out_26(screenconnector2_2_out_26), .out_27(screenconnector2_2_out_27),
    .out_28(screenconnector2_2_out_28), .out_29(screenconnector2_2_out_29),
    .out_30(screenconnector2_2_out_30), .out_31(screenconnector2_2_out_31),
    .out_32(screenconnector2_2_out_32), .out_33(screenconnector2_2_out_33),
    .out_34(screenconnector2_2_out_34), .out_35(screenconnector2_2_out_35),
    .out_36(screenconnector2_2_out_36), .Store(Controller_write), .Draw(Controller_draw));
  ROM #(.addrWidth(20), .dataWidth(32)) rom_3 (.addr(Controller_address), .data(rom_3_data));  // open: sel
  ROM #(.addrWidth(20), .dataWidth(32)) rom_4 (.addr(Controller_address), .data(rom_4_data));  // open: sel

  // Notes on the sheet:
  //   contents of rom_1 (hex, n*v repeats v):
  //   1202*0 18000000 18000000 30000000 38000000 30000000 70000000 60000000 e0000000 e0000000 e0000000
  //   c0000000 c0000000 c0000000 80000000 e0000000 5*80000000 10*0 1000000 1000000 2000000 2000000 0 0 0
  //   c000000 8000000 18000000 18000000 18000000 30000000 30000000 30000000 20000000 7*ff000000 8*fe000000
  //   fc000000 fc000200 fc000200 fc000400 fc000c00 fc000c00 fc000800 fc001800 fc001000 8*fc000000 ff800000
  //   ff800000 ffc00000 ffc00000 4*ffe00000 ffc00000 ffc00000 ff810000 ffc00000 6*ff800000 ff800080
  //   ff800080 ff800180 ff800100 ff800300 ff800300 ff000600 7*ff800000 ffe00000 4*fff00000 fff80000
  //   fff80000 7*fffc0000 11*fff80000 fff80010 fff80000 fff00000 4*fff80000 fffc0000 fffc0000 fffc0000
  //   fffe0000 fffe0000 fffe0000 ffff0000 6*ffff8000 ffff0000 ffff0000 ffff0000 5*ffff0400 7*ffff0000
  //   4*ffff8000 fffe0000 fffe0000 ffff0000 ffff0000 ffff0000 ffff8000 6*ffffc000 4*ffff8000 8*ffff8200
  //   ffff8000 ffff8000 ffffc000 ffffc800 ffffc800 6*ffffc000 ffffe000 ffffe000 6*fffff000 4*ffffe000
  //   ffffe080 ffffe080 ffffe1c0 ffffe1c0 5*ffffe180 ffffe100 fffff300 fffff300 fffff200 fffff200 fffff000
  //   fffff000 fffff000 ffffe000 ffffe000 fffff000 fffff000 6*fffff800 4*fffff000 9*fffff0c0 fffff080
  //   fffff980 fffff980 fffff980 fffff900 4*fffff800 fffffc00 fffffc00 8*fffffe00 7*fffffc00 4*fffffc20
  //   fffff820 fffffc20 fffffc60 fffffc60 fffffc40 fffffec0 4*fffffe00 fffffc00 fffffe00 fffffe00
  //   8*ffffff00 10*fffffe00 fffffc00 fffffc00 fffffe20 fffffe20 fffffe60 fffffe60 fffffe00 ffffff00
  //   ffffff00 ffffff00 fffffe00 fffffe00 ffffff80 ffffff80 ffffff80 ffffffc0 ffffffc0 ffffff80 ffffff80
  //   4*ffffffc0 9*ffffff80 ffffff00 ffffff00 ffffff00 ffffff80 ffffff90 ffffff90 6*ffffff80 fffffc00
  //   fffffe00 9*ffffffc0 ffffffe0 fffffff0 fffffff0 fffffff0 8*ffffffe0 ffffffc0 ffffffc0 ffffffc0
  //   6*ffffffe0 fffffc00 fffffc00 ffffff80 ffffff80 ffffff80 7*ffffffc0 ffffffe0 7*fffffff0 6*ffffffe0
  //   fffffff0 fffffff0 fffffff0 ffffffe0 ffffffc0 ffffffc0 fffff800 ffffff00 ffffff00 ffffff00 4*ffffff80
  //   ffffff00 ffffff00 ffffff80 ffffffc0 ffffffc0 ffffffe0 ffffffe0 ffffffe0 7*fffffff0 ffffffe0 fffffff0
  //   fffffff0 ffffffe0 ffffffc0 ffffff80 ffffff00 ffffff00 fffffe00 6*ffffff00 4*fffffe00 ffffff80
  //   ffffff80 ffffffc0 ffffffc0 ffffffc0 ffffffe0 ffffffe0 5*fffffff0 ffffffc0 ffffffe0 ffffffe0 ffffffc0
  //   ffffff80 ffffff00 fffffe00 fffffe00 fffffc00 fffffc00 fffffe00 fffffe00 fffffc00 fffffc00 fffffc00
  //   fffff800 fffff800 fffff800 fffffe00 ffffff00 ffffff00 ffffff00 ffffff80 ffffff80 ffffff80 ffffffc0
  //   ffffffc0 4*ffffffe0 ffffff80 ffffff80 ffffff80 ffffff00 fffffe00 fffffc00 fffffc00 fffff800 fffff800
  //   fffff800 fffff000 fffffe00 fffffc00 fffffc00 fffff800 fffff800 fffff000 fffff000 fffff800 fffffe00
  //   fffffe00 5*ffffff00 4*ffffff80 ffffffc0 ffffffc0 ffffff00 ffffff00 ffffff00 fffffe00 fffffc00
  //   fffff800 fffff800 4*fffff000 fffffe00 fffffe00 fffffc00 fffff800 fffff800 fffff000 fffff000 fffff000
  //   fffffc00 fffffe00 9*ffffff00 ffffff80 ffffff80 4*ffffff00 fffffc00 fffff800 fffff800 4*fffff000
  //   ffffe000 fffff000 fffffe00 fffffc00 fffffc00 fffff800 4*fffff000 14*fffffe00 ffffff00 fffffe00
  //   fffffc00 fffff800 fffff000 fffff000 5*ffffe000 fffffc00 fffffc00 fffff800 fffff800 fffff000 fffff000
  //   ffffe000 fffff000 9*fffffc00 6*fffffe00 fffffc00 fffff800 fffff000 fffff000 ffffe000 ffffe000
  //   ffffc000 ffffc000 ffffc000 ffffe000 fffffc00 fffffc00 fffff800 fffff800 fffff000 fffff000 ffffe000
  //   ffffe000 13*fffffc00 fffffe00 fffffc00 fffff800 fffff000 fffff000 ffffe000 ffffe000 ffffc000
  //   ffffc000 ffffc000 ffffe000 fffffc00 fffffc00 fffff800 fffff800 fffff000 fffff000 ffffe000 fffff000
  //   fffffc00 fffffc00 7*fffff800 6*fffffc00 fffff800 fffff000 ffffe000 ffffe000 ffffe000 4*ffffc000
  //   fffff800 fffff800 fffff000 fffff000 ffffe000 ffffe000 ffffe000 fffff000 14*fffff800 fffff000
  //   fffff000 ffffe000 ffffe000 ffffc000 ffffc000 ffff8000 ffff8000 ffff8000 ffffd000 fffff000 fffff000
  //   ffffe000 ffffe000 ffffc000 ffffc000 ffffc000 fffff000 4*fffff800 fffff000 fffff000 fffff000
  //   6*fffff800 fffff000 ffffe000 ffffe000 4*ffffc000 ffff8000 ffff8000 ffff8000 fffff000 fffff000
  //   ffffe000 ffffe000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
  //   contents of rom_2 (hex, n*v repeats v):
  //   1184*0 80000000 31*0 60000000 40000000 40000000 80000000 28*0 fc000000 fc000000 4*f8000000 f0000000
  //   f0000000 e0000000 e0000000 e0000000 c0000000 c0000000 4*80000000 15*0 ff800000 ff000000 ff000000
  //   ff000000 fe000000 fe000000 fc000000 fc000000 fc000000 f8000000 f8000000 f0000000 f0000000 4*e0000000
  //   c0000000 4*80000000 10*0 4*fff80000 fff00000 fff00000 ffe00000 ffe00000 ffc00000 ffc00000 ff800000
  //   ff800000 ff000000 ff000000 fe000000 fe000000 fe000000 fc000000 f8000000 f8000000 f8000000 f0000000
  //   f0000000 f0000000 4*e0000000 c0000000 c0000000 c0000000 80000000 ffff8000 ffff8000 ffff8000 ffff0000
  //   ffff0000 fffe0000 fffe0000 fffc0000 fffc0000 fff80000 fff80000 fff00000 fff00000 ffe00000 ffe00000
  //   ffe00000 ffc00000 ff800000 ff800000 ff800000 ff000000 ff000000 4*fe000000 fc000000 fc000000 fc000000
  //   f8000000 f8000000 f8000000 ffffc000 ffffc000 ffffc000 ffff8000 ffff8000 ffff0000 ffff0000 ffff0000
  //   fffe0000 fffe0000 fffc0000 fffc0000 fff80000 fff80000 fff80000 fff00000 ffe00000 ffe00000 ffe00000
  //   ffc00000 ffc00000 ff800000 ff800000 ff800000 ff000000 ff000000 ff000000 4*fe000000 fc000000 fffff000
  //   4*ffffe000 5*ffffc000 ffff8000 ffff8000 ffff0000 ffff0000 fffe0000 fffc0000 6*fff80000 fff00000
  //   fff00000 fff00000 ffe00000 ffe00000 ffe00000 4*ffc00000 fffff800 4*fffff000 5*ffffe000 ffffc000
  //   ffffc000 ffff0000 fffe0000 fffe0000 4*fffc0000 fffe0000 fffc0000 fffc0000 fffc0000 4*fff80000
  //   fff00000 fff00000 fff00000 ffe00000 ffe00000 6*fffffc00 fffff800 fffff800 fffff800 ffffe000 ffffc000
  //   7*ffff8000 ffffc000 ffffc000 ffff8000 ffff8000 4*ffff0000 4*fffe0000 fffc0000 fffc0000 5*fffffe00
  //   fffffc00 fffffc00 fffffc00 fffff000 ffffe000 6*ffffc000 ffffe000 ffffe000 ffffe000 4*ffffc000
  //   4*ffff8000 4*ffff0000 fffe0000 ffffff80 ffffff80 5*ffffff00 fffffc00 fffff000 fffff000 fffff000
  //   ffffe000 fffff000 fffff000 fffff000 4*fffff800 4*fffff000 ffffe000 ffffe000 ffffe000 ffffc000
  //   ffffc000 ffffc000 ffff8000 ffff8000 ffff8000 ffffffc0 ffffffc0 6*ffffff80 fffffe00 7*fffff800
  //   fffffc00 fffffc00 fffff800 fffff800 fffff800 fffff000 fffff000 fffff000 ffffe000 ffffe000 ffffe000
  //   ffffc000 ffffc000 ffffc000 ffff8000 ffff8000 5*ffffff80 ffffff00 ffffff00 ffffff00 fffffc00 fffff800
  //   4*fffff000 6*fffff800 fffff000 fffff000 fffff000 ffffe000 ffffe000 ffffe000 ffffc000 ffffc000
  //   ffffc000 ffff8000 ffff8000 ffff8000 7*fffffe00 fffff800 fffff000 4*ffffe000 7*fffff000 ffffe000
  //   ffffe000 ffffe000 ffffc000 ffffc000 ffffc000 ffff8000 ffff8000 ffff8000 ffff0000 ffff0000 ffff0000
  //   6*fffffc00 fffff800 ffffe000 ffffe000 ffffc000 ffffc000 ffffc000 ffffe000 fffff000 fffff000 fffff000
  //   5*ffffe000 ffffc000 ffffc000 ffffc000 ffff8000 ffff8000 ffff8000 ffff0000 ffff0000 ffff0000 fffe0000
  //   fffe0000 6*fffff000 ffffc000 4*ffff8000 8*ffffc000 4*ffff8000 ffff0000 ffff0000 ffff0000 fffe0000
  //   fffe0000 fffc0000 fffc0000 fffc0000 fff80000 fffff000 fffff000 fffff000 ffffe000 ffffe000 ffffe000
  //   ffff8000 ffff0000 ffff0000 ffff0000 7*ffff8000 4*ffff0000 fffe0000 fffe0000 fffe0000 fffc0000
  //   fffc0000 fffc0000 fff80000 fff80000 fff80000 fff00000 fff00000 fffff000 5*ffffe000 ffff8000 ffff0000
  //   ffff0000 ffff0000 4*ffff8000 5*ffff0000 fffe0000 fffe0000 fffe0000 fffc0000 fffc0000 fffc0000
  //   fff80000 fff80000 fff80000 fff00000 fff00000 fff00000 ffe00000 5*ffffe000 ffffc000 ffffc000 fffe0000
  //   fffe0000 6*ffff0000 4*fffe0000 fffc0000 fffc0000 fffc0000 fff80000 fff80000 fff80000 fff00000
  //   fff00000 fff00000 ffe00000 ffe00000 ffc00000 ffc00000 5*ffffe000 ffffc000 ffffc000 fffe0000 fffe0000
  //   fffe0000 4*ffff0000 4*fffe0000 fffc0000 fffc0000 fffc0000 fff80000 fff80000 fff80000 fff00000
  //   fff00000 fff00000 ffe00000 ffe00000 ffc00000 ffc00000 ffc00000 ffffe000 ffffe000 ffffe000 4*ffffc000
  //   fffe0000 fffe0000 fffe0000 ffff0000 ffff0000 ffff0000 fffe0000 fffe0000 fffe0000 4*fffc0000 fff80000
  //   fff80000 fff80000 fff00000 fff00000 ffe00000 ffe00000 ffe00000 ffc00000 ffc00000 ff800000 ff800000
  //   ffffe000 ffffe000 4*ffffc000 fffe8000 fffe0000 fffe0000 fffe0000 ffff0000 ffff0000 fffe0000 fffe0000
  //   fffe0000 4*fffc0000 fff80000 fff80000 fff00000 fff00000 fff00000 ffe0000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
  //   For FPS testing - store the current frame
  //   contents of rom_3 (hex, n*v repeats v):
  //   894*0 22*1 10*3 7 7 0 0 0 20 20 20 30 30 30 4*38 3c 3c 1c 1e 1e 1e 1f 1f 11*3f 25*0 10000 10000
  //   10000 18000 8180 580 580 3f 3f 3f 7*1f 6*f 4*7 3 3 1 1 7 7*1f 12*3ffff 14*1ffff 6*ffff 1fffff
  //   13*3fffff 10*1fffff 4*fffff 4*1fffff 3fffff 3fffff 3fffff 7fffff 7fffff 7fffff ffffff ffffff 1ffffff
  //   1ffffff 1ffffff 11*3ffffff 1ffffff 1ffffff ffffff 7fffff 7fffff ffffff ffffff 1ffffff 1ffffff
  //   3ffffff 7ffff 7ffff 7ffff fffff 4fffff 1fffff 1fffff 1fffff 3fffff 3fffff 7fffff 7fffff ffffff
  //   1ffffff 1ffffff 4*3ffffff 7ffffff 3fffff 3ffff 7ffff 7ffff 4*fffff 7ffff 3ffff 1ffff ffff 1ffff
  //   3ffff 3ffff 13ffff 7ffff 27ffff 2fffff 2fffff fffff 1fffff 7fffff 7fffff 7fffff ffffff ffffff ffffff
  //   1ffffff 1ffffff 1ffffff ffff 1ffff 1ffff 5*3ffff ffff 7fff 3fff 1fff fff 7fff ffff ffff 1ffff 1ffff
  //   1ffff 3ffff 3ffff 7ffff 7ffff 7ffff 4*fffff 1fffff 1fffff 1fffff 3fff 4*7fff ffff ffff 7fff 3fff fff
  //   7ff 3ff 3ff 1ff 7fff 7fff ffff ffff 6*1ffff 4*3ffff 7ffff 7ffff 7ffff fffff 7fff 3fff 4*7fff ffff
  //   7fff 3fff fff 7ff 3ff 3ff 1ff 9*3fff 6*7fff 5*ffff 3fff 3fff 3fff 4*7fff 3fff 1fff 7ff 3ff 3ff
  //   11*1fff 7*3fff 4*7fff 3fff 3fff 3fff 7fff 7fff 7fff 3fff fff 7ff 3ff 7f 7f ff 17*fff 4fff 4*5fff
  //   4*1fff 3fff 3fff 1fff ff ff ff 1ff 6*fff 8*7ff 17ff 17ff 17ff 9*1fff fff 7ff ff ff 1ff 5*fff 8*7ff
  //   3ff bff bff bff fff fff fff 7*7ff 3ff 1ff ff 1ff 7ff 5*fff 6*7ff 3ff 3ff 4*7ff 3ff 3ff 4*7ff 17ff
  //   3ff 3ff 1ff ff ff ff 1ff 7ff 7ff 7ff 4*fff 15*7ff 13ff 1bff 7ff 3ff 1ff ff 7f 7f ff 3ff 3ff 3ff
  //   4*7ff 12*fff 7ff 7ff 7ff fff fff 3ff 1ff ff 7f 3f 3f 3f ff 4*3ff 4*7ff 7*fff 1fff 1fff fff fff 7ff
  //   7ff 7ff fff 7ff 3ff ff 7f 7f 3f 3f 3f 7f 7f ff 1ff 5*3ff 7ff 7ff 7ff 4*fff 5*1fff 5*7ff 3ff ff 7f 7f
  //   3f 3f ff ff 1ff 1ff ff 1ff 1ff 3ff 5*7ff 17*fff 3ff 1ff 8*3ff 7ff 5*fff 1fff 1fff 8*fff 6*1fff 7ff
  //   3ff 1fff 1fff fff 5*1fff 6*3fff 9*1fff 6*3fff 1fff 1fff fff 6*3fff 7fff 7fff 7fff ffff 7fff 7fff
  //   8*3fff 1fff 1fff 3fff 3fff 3fff 4*7fff 3fff 1fff 1fff 7fff 5*ffff 1ffff 1ffff 3ffff 3ffff 3ffff
  //   1ffff 1ffff 7*ffff 7fff 5*ffff 1ffff 1ffff ffff ffff 7fff 7fff ffff ffff 1ffff 1ffff 4*3ffff 7ffff
  //   7ffff fffff fffff 4*7ffff 13*3ffff 1ffff 1ffff 1ffff ffff ffff 1ffff 1ffff 4*3ffff 7ffff 8*fffff
  //   12*7ffff 3ffff 3ffff 4*1ffff 3ffff 3ffff 7ffff 7ffff 4*fffff 1fffff 5*3fffff 12*1fffff fffff fffff
  //   7ffff 1ffff 1ffff 3ffff 3ffff 3ffff 7ffff 7ffff fffff fffff fffff 1fffff 1fffff 1fffff 3fffff 7fffff
  //   7fffff 7fffff 12*3fffff 1fffff 1fffff fffff 3ffff 3ffff 3ffff 7ffff 7ffff fffff fffff 1fffff 1fffff
  //   4*3fffff 7fffff 7fffff 9*ffffff 7fffff 7fffff ffffff ffffff 7fffff 7fffff 3fffff 3fffff 3ffff 3ffff
  //   7ffff 7ffff fffff fffff 1fffff 1fffff 4*3fffff 7fffff 7fffff ffffff ffffff 1ffffff 9*ffffff 1ffffff
  //   ffffff ffffff ffffff 7fffff 7fffff 7ffff fffff fffff fffff 1fffff 1fffff 3fffff 3fffff 4*7fffff
  //   ffffff 1ffffff 1ffffff 3ffffff 3ffffff 8*1ffffff 3ffffff 3ffffff 3ffffff 1ffffff ffffff ffffff
  //   ffffff 1fffff 1fffff 1fffff 3fffff 3fffff 7fffff 7fffff ffffff 5*1ffffff 3ffffff 3ffffff 7ffffff
  //   10*3ffffff 7ffffff 3ffffff 3ffffff 1ffffff 1ffffff 1ffffff 1fffff 3fffff 3fffff 3fffff 7fffff 7fffff
  //   ffffff ffffff 4*1ffffff 3ffffff 6*7ffffff 5*3ffffff 4*7ffffff 3ffffff 3ffffff 3ffffff 1ffffff 3fffff
  //   7fffff 7fffff ffffff ffffff ffffff 1ffffff 1ffffff 3ffffff 4*7ffffff 5*fffffff 6*7ffffff fffffff
  //   fffffff fffffff 4*7ffffff 3ffffff 7fffff 7fffff ffffff ffffff ffffff 1ffffff 1ffffff 3ffffff
  //   4*7ffffff fffffff fffffff 1fffffff 1fffffff 12*fffffff 4*7ffffff ffffff ffffff ffffff 4*1ffffff
  //   3ffffff 3ffffff 7ffffff 4*fffffff 1fffffff 1fffffff 3fffffff 3fffffff 10*1fffffff 4*fffffff ffffff
  //   ffffff ffffff 4*1ffffff 3ffffff 3ffffff 7ffffff 4*fffffff 1fffffff 1fffffff 4*3fffffff 5*1fffffff
  //   3fffffff 3fffffff 1fffffff 1fffffff fffffff fffffff fffffff 7fffff 4*ffffff 1ffffff 1ffffff 1ffffff
  //   3ffffff 3ffffff 5*fffffff 1fffffff 1fffffff 1fffffff 8*3fffffff fffffff fffffff 4*7ffffff 7fffff
  //   7fffff 7fffff 4*ffffff 1ffffff 7*7ffffff fffffff fffffff 1fffffff 1fffffff 3fffffff 3fffffff
  //   3fffffff fffffff 1fffffff fffffff 7ffffff 5*3ffffff 1ffffff 5*7fffff ffffff ffffff fffff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
  //   contents of rom_4 (hex, n*v repeats v):
  //   864*0 1 31*0 7 7 7 10*f 7 3 17*0 5*3f bf 5*ff 7f 3f 1f f 7 7 3 1 1 12*0 7c0 7c0 7c0 7e0 7e0 fe0 ff0
  //   1ff0 1ff0 1ff8 ff8 7f8 7fc 3fc 1fc 1fe 1fe ff ff 4*7f 9*3f 1000f 4*f 4*200f 300f 100f 100f 100f 807
  //   807 11*7 5*1f 3f ffff 3ffff 7ffff 7ffff 7ffff 7*3ffff 1ffff ffff ffff ffff 7fff 7fff 7fff 3fff 3fff
  //   1fff 1fff 1fff fff fff 4*7ff 3ff 3ff fffff fffff 8*1fffff fffff fffff 7ffff 7ffff 3ffff 3ffff 1ffff
  //   1ffff 1ffff ffff ffff 7fff 7fff 7fff 3fff 3fff 1fff 1fff 1fff fff 7ff 3ff 1ffffff 7fffff 3fffff
  //   1fffff fffff 3ffff 3ffff 1ffff ffff ffff 7fff 7fff 3fff 3fff 3fff 11*1fff 7ff 3ff 1ff ff 7f 7f 7fff
  //   3fff 1fff fff fff 7ff 7ff 3ff 3ff 3ff 14*1ff ff 7f 3f 1f f 7 7 7 7ff 7ff 3ff 1ff 1ff 5*ff 6*7f 7*ff
  //   7f 1f f 7 3 3 1 1 1 ff ff 7f 7f 18*3f 1f 7 3 1 6*0 ff ff 7f 7f 15*3f 4*1f 3 1 7*0 1ff ff ff 7f 7f
  //   11*3f 6*1f f 9*0 1ff 1ff ff 7f 7f 7f 10*3f 6*1f f 9*0 7ff 3ff 1ff 1ff ff 7f 7f 7f 8*3f 6*1f f 9*0
  //   3ff 1ff ff ff 4*7f 7*3f 5*1f f 11*0 1ff ff ff 4*7f 7*3f 5*1f 13*0 7f 7f 7f 8*3f 5*1f f 8*0 1 5*0 800
  //   8*3f 6*1f f f 7*0 1 1 0 0 0 4*800 3f 3f 8*1f 4*f 7*0 1 1 0 5*800 1800 1800 1800 9*1f 4*f 6*0 1 1 1
  //   801 800 800 800 6*1800 4*3f 8*1f f 1 0 0 0 1 4*3 1003 1003 1003 1001 1001 4*3001 3000 ff ff 12*7f 1f
  //   4*7 f f 7*1f f f 400f 400f 1ff 1ff 1ff 10*ff 7f 1f f f f 1f 10*3f 1f 1f 1f 11*7ff ff 7f 7f 7f ff ff
  //   1ff 201ff 201ff 601ff 5*600ff e00ff c00ff c007f c007f c007f c003f 5*1fff 5*fff 1ff ff ff 1ff 1ff 3ff
  //   403ff 4*c03ff 6*1c01ff 1c00ff 1c00ff 1c00ff 1c007f 1c007f 5*7fff 3fff 203fff 203fff 200fff 7ff
  //   2007ff fff fff 201fff 301fff 301fff 6*700fff 4*f007ff 7003ff 7003ff 7003ff 7001ff 7001ff 7001ff
  //   4*ffff 7fff 7fff 7fff 3fff 3fff 1fff 3fff 3fff 3fff 5*c01fff 9*1c01fff 1c00fff 1c00fff 1c00fff
  //   1c007ff 1c007ff 1ffff 1ffff ffff ffff ffff 4*7fff 4*3fff 803fff 803fff 803fff 1803fff 13*1801fff
  //   1800fff 1800fff 7ffff 3ffff 3ffff 3ffff 1ffff 1ffff 1ffff ffff ffff ffff 6*7fff 3fff 4*2003fff
  //   4*6003fff 7*2003fff fffff 7ffff 7ffff 3ffff 3ffff 3ffff 1ffff 1ffff 1ffff 4*ffff 7fff 7fff 7fff
  //   47fff 47fff 47fff 4047fff 4043fff 9*4003fff 6003fff 6003fff 1fffff 1fffff 1fffff fffff fffff 7ffff
  //   7ffff 7ffff 3ffff 3ffff 3ffff 1ffff 1ffff 11ffff 11ffff 10ffff 10ffff 8ffff 8ffff 8ffff 808ffff
  //   7*8007fff 7fff 7fff 7fff 4003fff 3fffff 3fffff 1fffff 1fffff fffff fffff fffff 7ffff 7ffff 7ffff
  //   4*3ffff 1ffff 11ffff 11ffff 11ffff 10ffff 7*ffff 6*7fff 7fffff 7fffff 7fffff 3fffff 3fffff 1fffff
  //   1fffff 1fffff fffff fffff fffff 4*7ffff 6*3ffff 6*1ffff 4*ffff 2ffff 1ffffff ffffff ffffff 7fffff
  //   7fffff 4*3fffff 4*1fffff 5*fffff 5*7ffff 7*3ffff 7ffff 7ffff 1ffffff 1ffffff ffffff ffffff 4*7fffff
  //   4*3fffff 4*1fffff 5*fffff 6*7ffff 3ffff 7ffff fffff 7ffff 7ffff 3ffffff 3ffffff 7*ffffff 5*7fffff
  //   5*3fffff 1fffff 1fffff 1fffff 9*fffff 7ffff 3ffffff 3ffffff 1ffffff ffffff ffffff 1ffffff 1ffffff
  //   1ffffff 4*ffffff 4*7fffff 4*3fffff 1fffff 1fffff 1fffff fffff fffff fffff 1fffff 1fffff fffff fffff
  //   fffff 7ffff fffffff 7ffffff 4*1ffffff 3ffffff 1ffffff 1ffffff 1ffffff 4*ffffff 7fffff 7fffff 7fffff
  //   3fffff 3fffff 3fffff 1fffff 1fffff 1fffff fffff 4*1fffff 4*fffff fffffff 7ffffff 8*1ffffff ffffff
  //   ffffff ffffff 4*7fffff 3fffff 3fffff 3fffff 1fffff 1fffff fffff fffff 4*1fffff 4*fffff 7ffffff
  //   3ffffff ffffff ffffff ffffff 1ffffff 1ffffff 1ffffff 4*ffffff 7fffff 7fffff 7fffff 3fffff 3fffff
  //   3fffff 1fffff 1fffff 1fffff fffff fffff fffff 1fffff 1fffff 1fffff 5*fffff 1ffffff ffffff 7fffff
  //   7fffff 4*ffffff 4*7fffff 4*3fffff 1fffff 1fffff 1fffff fffff fffff 7ffff 7ffff 8*fffff 1fffff
  //   1ffffff 10*7fffff 3fffff 3fffff 3fffff 1fffff 1fffff 1fffff fffff fffff fffff 4*7ffff fffff fffff
  //   fffff 7ffff 7ffff 7ffff fffff 1fffff ffffff 4*3fffff 7fffff 5*3fffff 1fffff 1fffff 1fffff fffff
  //   fffff fffff 7ffff 7ffff 7ffff 4*3ffff 4*7ffff 3ffff 7ffff 7ffff 7ffff 7fffff 3fffff 1fffff 5*3fffff
  //   4*1fffff 4*fffff 7ffff 7ffff 7ffff 12*3ffff 7ffff 7fffff 7fffff 7*1fffff 4*fffff 7ffff 7ffff 7ffff
  //   3ffff 3ffff 3ffff 12*1ffff 3ffff 7fffff 3fffff 1fffff fffff 1fffff 1fffff 1fffff 4*fffff 7ffff 7ffff
  //   7ffff 3ffff 3ffff 3ffff 1ffff 1ffff 1ffff 11*ffff 1ffff 3fffff 3fffff 3ff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
endmodule

module pixelmem (
  input  [31:0] Data,
  input  Store,
  input  Draw,
  output [31:0] PixelOut
);

  wire [31:0] register_1_q;

  Register #(.width(32)) register_1 (.D(Data), .Q(register_1_q), .clk(Store));  // open: en, clr
  Register #(.width(32)) register_2 (.D(register_1_q), .Q(PixelOut), .clk(Draw));  // open: en, clr
endmodule

module player (
  output [4:0] Row,
  output Draw,
  output [19:0] Address,
  output Write
);

  wire clock_1_out;

  Counter #(.width(5), .max('h1f)) counter_1 (.Q(Row), .clk(clock_1_out));  // open: load, D, count, carry, clr
  Counter #(.width(20), .max('hfffff)) counter_2 (.Q(Address), .clk(clock_1_out));  // open: load, D, count, carry, clr
  Clock clock_1 (.out(clock_1_out));
  not not_1 (Write, clock_1_out);
  Comparator #(.width(5), .mode("unsigned")) comparator_1 (.a(Row), .b({5{1'b0}}), .eq(Draw));  // open: gt, lt
endmodule

module screenconnector (
  input  [31:0] Data,
  input  Draw,
  input  Store,
  input  [4:0] Row,
  output [31:0] out_5,
  output [31:0] out_6,
  output [31:0] out_7,
  output [31:0] out_8,
  output [31:0] out_9,
  output [31:0] out_10,
  output [31:0] out_11,
  output [31:0] out_12,
  output [31:0] out_13,
  output [31:0] out_14,
  output [31:0] out_15,
  output [31:0] out_16,
  output [31:0] out_17,
  output [31:0] out_18,
  output [31:0] out_19,
  output [31:0] out_20,
  output [31:0] out_21,
  output [31:0] out_22,
  output [31:0] out_23,
  output [31:0] out_24,
  output [31:0] out_25,
  output [31:0] out_26,
  output [31:0] out_27,
  output [31:0] out_28,
  output [31:0] out_29,
  output [31:0] out_30,
  output [31:0] out_31,
  output [31:0] out_32,
  output [31:0] out_33,
  output [31:0] out_34,
  output [31:0] out_35,
  output [31:0] out_36
);

  wire demultiplexer_1_out0, demultiplexer_1_out1, demultiplexer_1_out2, demultiplexer_1_out3,
       demultiplexer_1_out4, demultiplexer_1_out5, demultiplexer_1_out6, demultiplexer_1_out7,
       demultiplexer_1_out8, demultiplexer_1_out9, demultiplexer_1_out10, demultiplexer_1_out11,
       demultiplexer_1_out12, demultiplexer_1_out13, demultiplexer_1_out14, demultiplexer_1_out15,
       demultiplexer_1_out16, demultiplexer_1_out17, demultiplexer_1_out18, demultiplexer_1_out19,
       demultiplexer_1_out20, demultiplexer_1_out21, demultiplexer_1_out22, demultiplexer_1_out23,
       demultiplexer_1_out24, demultiplexer_1_out25, demultiplexer_1_out26, demultiplexer_1_out27,
       demultiplexer_1_out28, demultiplexer_1_out29, demultiplexer_1_out30, demultiplexer_1_out31;

  Demultiplexer #(.select(5)) demultiplexer_1 (
    .out0(demultiplexer_1_out0), .out1(demultiplexer_1_out1), .out2(demultiplexer_1_out2),
    .out3(demultiplexer_1_out3), .out4(demultiplexer_1_out4), .out5(demultiplexer_1_out5),
    .out6(demultiplexer_1_out6), .out7(demultiplexer_1_out7), .out8(demultiplexer_1_out8),
    .out9(demultiplexer_1_out9), .out10(demultiplexer_1_out10), .out11(demultiplexer_1_out11),
    .out12(demultiplexer_1_out12), .out13(demultiplexer_1_out13), .out14(demultiplexer_1_out14),
    .out15(demultiplexer_1_out15), .out16(demultiplexer_1_out16), .out17(demultiplexer_1_out17),
    .out18(demultiplexer_1_out18), .out19(demultiplexer_1_out19), .out20(demultiplexer_1_out20),
    .out21(demultiplexer_1_out21), .out22(demultiplexer_1_out22), .out23(demultiplexer_1_out23),
    .out24(demultiplexer_1_out24), .out25(demultiplexer_1_out25), .out26(demultiplexer_1_out26),
    .out27(demultiplexer_1_out27), .out28(demultiplexer_1_out28), .out29(demultiplexer_1_out29),
    .out30(demultiplexer_1_out30), .out31(demultiplexer_1_out31), .in(Store), .sel(Row));  // open: en
  pixelmem pixelmem_1 (.Data(Data), .Store(demultiplexer_1_out0), .PixelOut(out_5), .Draw(Draw));
  pixelmem pixelmem_2 (.Data(Data), .Store(demultiplexer_1_out1), .PixelOut(out_6), .Draw(Draw));
  pixelmem pixelmem_3 (.Data(Data), .Store(demultiplexer_1_out2), .PixelOut(out_7), .Draw(Draw));
  pixelmem pixelmem_4 (.Data(Data), .Store(demultiplexer_1_out3), .PixelOut(out_8), .Draw(Draw));
  pixelmem pixelmem_5 (.Data(Data), .Store(demultiplexer_1_out4), .PixelOut(out_9), .Draw(Draw));
  pixelmem pixelmem_6 (.Data(Data), .Store(demultiplexer_1_out5), .PixelOut(out_10), .Draw(Draw));
  pixelmem pixelmem_7 (.Data(Data), .Store(demultiplexer_1_out6), .PixelOut(out_11), .Draw(Draw));
  pixelmem pixelmem_8 (.Data(Data), .Store(demultiplexer_1_out7), .PixelOut(out_12), .Draw(Draw));
  pixelmem pixelmem_9 (.Data(Data), .Store(demultiplexer_1_out8), .PixelOut(out_13), .Draw(Draw));
  pixelmem pixelmem_10 (.Data(Data), .Store(demultiplexer_1_out9), .PixelOut(out_14), .Draw(Draw));
  pixelmem pixelmem_11 (.Data(Data), .Store(demultiplexer_1_out10), .PixelOut(out_15), .Draw(Draw));
  pixelmem pixelmem_12 (.Data(Data), .Store(demultiplexer_1_out11), .PixelOut(out_16), .Draw(Draw));
  pixelmem pixelmem_13 (.Data(Data), .Store(demultiplexer_1_out12), .PixelOut(out_17), .Draw(Draw));
  pixelmem pixelmem_14 (.Data(Data), .Store(demultiplexer_1_out13), .PixelOut(out_18), .Draw(Draw));
  pixelmem pixelmem_15 (.Data(Data), .Store(demultiplexer_1_out14), .PixelOut(out_19), .Draw(Draw));
  pixelmem pixelmem_16 (.Data(Data), .Store(demultiplexer_1_out15), .PixelOut(out_20), .Draw(Draw));
  pixelmem pixelmem_17 (.Data(Data), .Store(demultiplexer_1_out16), .PixelOut(out_21), .Draw(Draw));
  pixelmem pixelmem_18 (.Data(Data), .Store(demultiplexer_1_out17), .PixelOut(out_22), .Draw(Draw));
  pixelmem pixelmem_19 (.Data(Data), .Store(demultiplexer_1_out18), .PixelOut(out_23), .Draw(Draw));
  pixelmem pixelmem_20 (.Data(Data), .Store(demultiplexer_1_out19), .PixelOut(out_24), .Draw(Draw));
  pixelmem pixelmem_21 (.Data(Data), .Store(demultiplexer_1_out20), .PixelOut(out_25), .Draw(Draw));
  pixelmem pixelmem_22 (.Data(Data), .Store(demultiplexer_1_out21), .PixelOut(out_26), .Draw(Draw));
  pixelmem pixelmem_23 (.Data(Data), .Store(demultiplexer_1_out22), .PixelOut(out_27), .Draw(Draw));
  pixelmem pixelmem_24 (.Data(Data), .Store(demultiplexer_1_out23), .PixelOut(out_28), .Draw(Draw));
  pixelmem pixelmem_25 (.Data(Data), .Store(demultiplexer_1_out24), .PixelOut(out_29), .Draw(Draw));
  pixelmem pixelmem_26 (.Data(Data), .Store(demultiplexer_1_out25), .PixelOut(out_30), .Draw(Draw));
  pixelmem pixelmem_27 (.Data(Data), .Store(demultiplexer_1_out26), .PixelOut(out_31), .Draw(Draw));
  pixelmem pixelmem_28 (.Data(Data), .Store(demultiplexer_1_out27), .PixelOut(out_32), .Draw(Draw));
  pixelmem pixelmem_29 (.Data(Data), .Store(demultiplexer_1_out28), .PixelOut(out_33), .Draw(Draw));
  pixelmem pixelmem_30 (.Data(Data), .Store(demultiplexer_1_out29), .PixelOut(out_34), .Draw(Draw));
  pixelmem pixelmem_31 (.Data(Data), .Store(demultiplexer_1_out30), .PixelOut(out_35), .Draw(Draw));
  pixelmem pixelmem_32 (.Data(Data), .Store(demultiplexer_1_out31), .PixelOut(out_36), .Draw(Draw));
endmodule

module screenconnector2 (
  input  [31:0] Data,
  input  Draw,
  input  Store,
  input  [4:0] Row,
  output [31:0] out_5,
  output [31:0] out_6,
  output [31:0] out_7,
  output [31:0] out_8,
  output [31:0] out_9,
  output [31:0] out_10,
  output [31:0] out_11,
  output [31:0] out_12,
  output [31:0] out_13,
  output [31:0] out_14,
  output [31:0] out_15,
  output [31:0] out_16,
  output [31:0] out_17,
  output [31:0] out_18,
  output [31:0] out_19,
  output [31:0] out_20,
  output [31:0] out_21,
  output [31:0] out_22,
  output [31:0] out_23,
  output [31:0] out_24,
  output [31:0] out_25,
  output [31:0] out_26,
  output [31:0] out_27,
  output [31:0] out_28,
  output [31:0] out_29,
  output [31:0] out_30,
  output [31:0] out_31,
  output [31:0] out_32,
  output [31:0] out_33,
  output [31:0] out_34,
  output [31:0] out_35,
  output [31:0] out_36
);

  wire demultiplexer_1_out0, demultiplexer_1_out1, demultiplexer_1_out2, demultiplexer_1_out3,
       demultiplexer_1_out4, demultiplexer_1_out5, demultiplexer_1_out6, demultiplexer_1_out7,
       demultiplexer_1_out8, demultiplexer_1_out9, demultiplexer_1_out10, demultiplexer_1_out11,
       demultiplexer_1_out12, demultiplexer_1_out13, demultiplexer_1_out14, demultiplexer_1_out15,
       demultiplexer_1_out16, demultiplexer_1_out17, demultiplexer_1_out18, demultiplexer_1_out19,
       demultiplexer_1_out20, demultiplexer_1_out21, demultiplexer_1_out22, demultiplexer_1_out23,
       demultiplexer_1_out24, demultiplexer_1_out25, demultiplexer_1_out26, demultiplexer_1_out27,
       demultiplexer_1_out28, demultiplexer_1_out29, demultiplexer_1_out30, demultiplexer_1_out31;

  Demultiplexer #(.select(5)) demultiplexer_1 (
    .out0(demultiplexer_1_out0), .out1(demultiplexer_1_out1), .out2(demultiplexer_1_out2),
    .out3(demultiplexer_1_out3), .out4(demultiplexer_1_out4), .out5(demultiplexer_1_out5),
    .out6(demultiplexer_1_out6), .out7(demultiplexer_1_out7), .out8(demultiplexer_1_out8),
    .out9(demultiplexer_1_out9), .out10(demultiplexer_1_out10), .out11(demultiplexer_1_out11),
    .out12(demultiplexer_1_out12), .out13(demultiplexer_1_out13), .out14(demultiplexer_1_out14),
    .out15(demultiplexer_1_out15), .out16(demultiplexer_1_out16), .out17(demultiplexer_1_out17),
    .out18(demultiplexer_1_out18), .out19(demultiplexer_1_out19), .out20(demultiplexer_1_out20),
    .out21(demultiplexer_1_out21), .out22(demultiplexer_1_out22), .out23(demultiplexer_1_out23),
    .out24(demultiplexer_1_out24), .out25(demultiplexer_1_out25), .out26(demultiplexer_1_out26),
    .out27(demultiplexer_1_out27), .out28(demultiplexer_1_out28), .out29(demultiplexer_1_out29),
    .out30(demultiplexer_1_out30), .out31(demultiplexer_1_out31), .in(Store), .sel(Row));  // open: en
  pixelmem pixelmem_1 (.Data(Data), .Store(demultiplexer_1_out0), .PixelOut(out_5), .Draw(Draw));
  pixelmem pixelmem_2 (.Data(Data), .Store(demultiplexer_1_out1), .PixelOut(out_6), .Draw(Draw));
  pixelmem pixelmem_3 (.Data(Data), .Store(demultiplexer_1_out2), .PixelOut(out_7), .Draw(Draw));
  pixelmem pixelmem_4 (.Data(Data), .Store(demultiplexer_1_out3), .PixelOut(out_8), .Draw(Draw));
  pixelmem pixelmem_5 (.Data(Data), .Store(demultiplexer_1_out4), .PixelOut(out_9), .Draw(Draw));
  pixelmem pixelmem_6 (.Data(Data), .Store(demultiplexer_1_out5), .PixelOut(out_10), .Draw(Draw));
  pixelmem pixelmem_7 (.Data(Data), .Store(demultiplexer_1_out6), .PixelOut(out_11), .Draw(Draw));
  pixelmem pixelmem_8 (.Data(Data), .Store(demultiplexer_1_out7), .PixelOut(out_12), .Draw(Draw));
  pixelmem pixelmem_9 (.Data(Data), .Store(demultiplexer_1_out8), .PixelOut(out_13), .Draw(Draw));
  pixelmem pixelmem_10 (.Data(Data), .Store(demultiplexer_1_out9), .PixelOut(out_14), .Draw(Draw));
  pixelmem pixelmem_11 (.Data(Data), .Store(demultiplexer_1_out10), .PixelOut(out_15), .Draw(Draw));
  pixelmem pixelmem_12 (.Data(Data), .Store(demultiplexer_1_out11), .PixelOut(out_16), .Draw(Draw));
  pixelmem pixelmem_13 (.Data(Data), .Store(demultiplexer_1_out12), .PixelOut(out_17), .Draw(Draw));
  pixelmem pixelmem_14 (.Data(Data), .Store(demultiplexer_1_out13), .PixelOut(out_18), .Draw(Draw));
  pixelmem pixelmem_15 (.Data(Data), .Store(demultiplexer_1_out14), .PixelOut(out_19), .Draw(Draw));
  pixelmem pixelmem_16 (.Data(Data), .Store(demultiplexer_1_out15), .PixelOut(out_20), .Draw(Draw));
  pixelmem pixelmem_17 (.Data(Data), .Store(demultiplexer_1_out16), .PixelOut(out_21), .Draw(Draw));
  pixelmem pixelmem_18 (.Data(Data), .Store(demultiplexer_1_out17), .PixelOut(out_22), .Draw(Draw));
  pixelmem pixelmem_19 (.Data(Data), .Store(demultiplexer_1_out18), .PixelOut(out_23), .Draw(Draw));
  pixelmem pixelmem_20 (.Data(Data), .Store(demultiplexer_1_out19), .PixelOut(out_24), .Draw(Draw));
  pixelmem pixelmem_21 (.Data(Data), .Store(demultiplexer_1_out20), .PixelOut(out_25), .Draw(Draw));
  pixelmem pixelmem_22 (.Data(Data), .Store(demultiplexer_1_out21), .PixelOut(out_26), .Draw(Draw));
  pixelmem pixelmem_23 (.Data(Data), .Store(demultiplexer_1_out22), .PixelOut(out_27), .Draw(Draw));
  pixelmem pixelmem_24 (.Data(Data), .Store(demultiplexer_1_out23), .PixelOut(out_28), .Draw(Draw));
  pixelmem pixelmem_25 (.Data(Data), .Store(demultiplexer_1_out24), .PixelOut(out_29), .Draw(Draw));
  pixelmem pixelmem_26 (.Data(Data), .Store(demultiplexer_1_out25), .PixelOut(out_30), .Draw(Draw));
  pixelmem pixelmem_27 (.Data(Data), .Store(demultiplexer_1_out26), .PixelOut(out_31), .Draw(Draw));
  pixelmem pixelmem_28 (.Data(Data), .Store(demultiplexer_1_out27), .PixelOut(out_32), .Draw(Draw));
  pixelmem pixelmem_29 (.Data(Data), .Store(demultiplexer_1_out28), .PixelOut(out_33), .Draw(Draw));
  pixelmem pixelmem_30 (.Data(Data), .Store(demultiplexer_1_out29), .PixelOut(out_34), .Draw(Draw));
  pixelmem pixelmem_31 (.Data(Data), .Store(demultiplexer_1_out30), .PixelOut(out_35), .Draw(Draw));
  pixelmem pixelmem_32 (.Data(Data), .Store(demultiplexer_1_out31), .PixelOut(out_36), .Draw(Draw));
endmodule
